# Fritzing sketch Design (saved by Fritzing 0.9.0b)
breadboards: 1

parts:
  IC1 = IC, DIP package, 20 pins [chip_label=PIC18F14K22 part_number=PIC18F14K22]
  Part1 = Triple Axis Magnetometer - HMC5883 Breakout
  R1 = Resistor [tolerance=±5% resistance=3.3k package=THT]
  R2 = Resistor [tolerance=±5% resistance=3.3k package=THT]
  D2 = Rectifier Diode [part_number=1N4001 package="300 mil [THT]"]
  U10 = Vibration Motor- ROB-08449 [package=vibe-motor-10mm]
  Q10 = NPN-Transistor [package="TO92 [THT]"]
  D3 = Rectifier Diode [part_number=1N4001 package="300 mil [THT]"]
  U11 = Vibration Motor- ROB-08449 [package=vibe-motor-10mm]
  Q11 = NPN-Transistor [package="TO92 [THT]"]
  D4 = Rectifier Diode [part_number=1N4001 package="300 mil [THT]"]
  U12 = Vibration Motor- ROB-08449 [package=vibe-motor-10mm]
  Q12 = NPN-Transistor [package="TO92 [THT]"]
  D5 = Rectifier Diode [part_number=1N4001 package="300 mil [THT]"]
  U13 = Vibration Motor- ROB-08449 [package=vibe-motor-10mm]
  Q13 = NPN-Transistor [package="TO92 [THT]"]
  D6 = Rectifier Diode [part_number=1N4001 package="300 mil [THT]"]
  D7 = Rectifier Diode [part_number=1N4001 package="300 mil [THT]"]
  D8 = Rectifier Diode [part_number=1N4001 package="300 mil [THT]"]
  D9 = Rectifier Diode [part_number=1N4001 package="300 mil [THT]"]
  U14 = Vibration Motor- ROB-08449 [package=vibe-motor-10mm]
  U15 = Vibration Motor- ROB-08449 [package=vibe-motor-10mm]
  U16 = Vibration Motor- ROB-08449 [package=vibe-motor-10mm]
  U17 = Vibration Motor- ROB-08449 [package=vibe-motor-10mm]
  Q14 = NPN-Transistor [package="TO92 [THT]"]
  Q15 = NPN-Transistor [package="TO92 [THT]"]
  Q16 = NPN-Transistor [package="TO92 [THT]"]
  Q17 = NPN-Transistor [package="TO92 [THT]"]
  VCC1 = Battery

nets:
  N1: IC1.pin1, Part1.VCC, R1.Pin_1, R2.Pin_1, D2.cathode, U10.-, D3.cathode, U11.-, D4.cathode, U12.-, D5.cathode, U13.-, D6.cathode, D7.cathode, D8.cathode, D9.cathode, U14.-, U15.-, U16.-, U17.-, VCC1.+
  N2: IC1.pin5, Q14.B
  N3: IC1.pin6, Q13.B
  N4: IC1.pin7, Q11.B
  N5: IC1.pin8, Q10.B
  N6: IC1.pin9, Q12.B
  N7: IC1.pin11, Part1.SCL, R2.Pin_0
  N8: IC1.pin13, Part1.SDA, R1.Pin_0
  N9: IC1.pin14, Q16.B
  N10: IC1.pin15, Q15.B
  N11: IC1.pin16, Q17.B
  N12: IC1.pin20, Part1.GND, Q10.E, Q11.E, Q12.E, Q13.E, Q14.E, Q15.E, Q16.E, Q17.E, VCC1.-
  N13: D2.anode, U10.+, Q10.C
  N14: D3.anode, U11.+, Q11.C
  N15: D4.anode, U12.+, Q12.C
  N16: D5.anode, U13.+, Q13.C
  N17: D6.anode, U16.+, Q17.C
  N18: D7.anode, U14.+, Q16.C
  N19: D8.anode, U15.+, Q15.C
  N20: D9.anode, U17.+, Q14.C

notes:
  RED WIRES: high current
  BLUE WIRES: low current
